// Digital circuit lc3-acv.dig as structural Verilog
module lc3_acv (
  input  mode,
  input  [3:0] opcode,
  input  [2:0] nzp,
  output ACV
);

  wire and_1_out, and_2_out, or_1_out;

  and and_1 (and_1_out, ~opcode[3], ~opcode[2]);  // And
  and and_2 (and_2_out, opcode[3], opcode[2], opcode[1], opcode[0], nzp[2], nzp[1], nzp[0]);
  or or_1 (or_1_out, and_1_out, and_2_out);
  and and_3 (ACV, mode, or_1_out);
endmodule
