// Digital circuit lc3-halt_HDL.dig as structural Verilog
module lc3_halt_HDL (
  input  [15:0] MAR,
  input  [15:0] D_in,
  input  R_W,
  output Run
);

  wire comparator_1_eq;

  Comparator #(.Bits(16)) comparator_1 (.a(MAR), .b(16'hfffe), .eq(comparator_1_eq));  // open: gt, lt
  nand nand_1 (Run, comparator_1_eq, R_W, ~D_in[15]);  // NAnd
  // Pins of 1 and 16 bits meet at MAR
  // Pins of 1 and 16 bits meet at D_in
endmodule
