// Digital circuit lc3-memmap.dig as structural Verilog
module lc3_memmap (
  input  [15:0] addr,
  input  en,
  input  R,
  output MEM_EN,
  output [1:0] MDR_Select
);

  Comparator comparator_1 (.a(addr[0]), .b(1'b0));  // open: gt, eq, lt
  Comparator comparator_2 (.a(addr[0]), .b(1'b0));  // open: gt, eq, lt
  Comparator comparator_3 (.a(addr[0]), .b(1'b0));  // open: gt, eq, lt
  Comparator comparator_4 (.a(addr[0]), .b(1'b0));  // open: gt, eq, lt
  // Pins of 1 and 16 bits meet at addr
  // Pins of 1 and 16 bits meet at 16'hfe00
  // Pins of 1 and 16 bits meet at 16'hfe02
  // Pins of 1 and 16 bits meet at 16'hfe04
  // Pins of 1 and 16 bits meet at 16'hfe06
endmodule
