// Digital circuit lc3-memory.dig as structural Verilog
module lc3_memory (
  input  [15:0] Addr,
  input  [15:0] D_in,
  input  MEM_EN,
  input  R_W,
  input  Clk,
  output [15:0] D_out,
  output [2:0] R
);

  wire and_1_out, and_2_out, or_1_out;

  and and_1 (and_1_out, MEM_EN, R_W);
  and and_2 (and_2_out, MEM_EN, ~R_W);  // And
  RAMDualPort #(.AddrBits(16), .isProgramMemory("true"), .Bits(16)) ramdualport_1 (
    .A(Addr), .Din(D_in), .str(and_1_out), .C(Clk), .ld(1'b1), .D(D_out));
  or or_1 (or_1_out, and_2_out, and_1_out);
  CounterPreset #(.maxValue(4), .Bits(3)) counterpreset_1 (
    .en(1'b1), .C(Clk), .dir(1'b0), .in(3'b000), .ld(1'b0), .clr(~or_1_out), .ovf(R[0]));  // open: out
  // Pins of 1 and 3 bits meet at R
endmodule
