// Digital circuit lc3.dig as structural Verilog
module lc3 (
  input  Clk,
  input  [15:0] Breakpoint
);

  wire ACV, ADDR1MUX, and_1_out, and_2_out, BEN, comparator_1_eq, comparator_2_eq, comparator_3_eq,
       comparator_4_eq, GateALU, GateMARMUX, GateMDR, GatePC, GatePC_1, GatePSR, GateSP, GateVector,
       lc3_cc_logic_1_n, lc3_cc_logic_1_p, lc3_cc_logic_1_z, LD_ACV, LD_BEN, LD_CC, LD_DDR, LD_DSR, LD_IR,
       LD_KBSR, LD_MAR, LD_MDR, LD_PC, LD_Priv, LD_REG, LD_SavedSSP, LD_SavedUSP, LD_Vector, MARMUX, MEM_EN,
       MIO_EN, N, P, PSR_15, PSRMux, R, R_mapped, R_mem, R_W, Set_Priv, SR2MUX, TableMux, Z;
  wire [1:0] ADDR2MUX, ALUK, DRMUX, MDR_Select, PCMUX, SPMUX, SR1MUX;
  wire [2:0] DR_nzp, multiplexer_7_out, multiplexer_9_out, SR1;
  wire [4:0] Immed;
  wire [4:1] IR_15_11;
  wire [5:0] State;
  wire [15:0] _1_s, D_in, D_out, driver_1_out, DSR, INMUX_out, KBDR, KBSR, keyboard_1_d, lc3_alu_1_alu,
       lc3_alu_2_alu, lc3_register_file_1_sr2_out, MAR, multiplexer_1_out, multiplexer_2_out,
       multiplexer_3_out, multiplexer_4_out, multiplexer_6_out, multiplexer_8_out, PC, plus_1_s, SEXT_2_out,
       SEXT_3_out, SEXT_4_out, SEXT_out, SR1_OUT;
  wire [15:15] KB_Data;

  Comparator #(.Bits(16)) comparator_1 (.a(Breakpoint), .b(PC), .eq(comparator_1_eq));  // open: gt, lt
  Comparator #(.Bits(6)) comparator_2 (.a(State), .b(6'b010010), .eq(comparator_2_eq));  // open: gt, lt
  Comparator #(.Bits(16)) comparator_3 (.a(MAR), .b(16'hfffe), .eq(comparator_3_eq));  // open: gt, lt
  and and_1 (and_1_out, comparator_1_eq, comparator_2_eq);
  and and_2 (and_2_out, comparator_3_eq, R_W, ~D_in[15]);  // And
  Break break_1 (.brk(and_1_out));
  Stop stop_1 (.stop(and_2_out));
  Register #(.Bits(16)) IR (.D(driver_1_out), .C(Clk), .en(LD_IR), .Q({IR_15_11, DR_nzp, SR1, SR2MUX, Immed}));
  BitExtender #(.inputBits(6)) SEXT (.in({SR2MUX, Immed}), .out(SEXT_out));
  BitExtender #(.inputBits(9)) SEXT_2 (.in({SR1, SR2MUX, Immed}), .out(SEXT_2_out));
  BitExtender #(.inputBits(11)) SEXT_3 (.in({DR_nzp[1:0], SR1, SR2MUX, Immed}), .out(SEXT_3_out));
  assign driver_1_out = GateMARMUX ? multiplexer_1_out : 16'bz;  // Driver driver_1
  Multiplexer #(.Bits(16)) multiplexer_1 (
    .sel(MARMUX), .in_0({{8{1'b0}}, SR1[1:0], SR2MUX, Immed}), .in_1(lc3_alu_1_alu), .out(multiplexer_1_out));
  or or_1 (R, R_mem, R_mapped);
  Multiplexer #(.Selector_Bits(2), .Bits(16)) multiplexer_2 (
    .sel(ADDR2MUX), .in_0({16{1'b0}}), .in_1(SEXT_out), .in_2(SEXT_2_out), .in_3(SEXT_3_out),
    .out(multiplexer_2_out));
  Multiplexer #(.Bits(16)) multiplexer_3 (.sel(ADDR1MUX), .in_0(PC), .in_1(SR1_OUT), .out(multiplexer_3_out));
  LED u_N (.in(N));
  Register N_2 (.D(lc3_cc_logic_1_n), .C(Clk), .en(LD_CC), .Q(N));
  lc3_alu lc3_alu_1 (.ALU(lc3_alu_1_alu), .A(multiplexer_2_out), .B(multiplexer_3_out), .ALUK(2'b00));
  Register u_Z (.D(lc3_cc_logic_1_z), .C(Clk), .en(LD_CC), .Q(Z));
  lc3_cc_logic lc3_cc_logic_1 (.D_in(driver_1_out), .N(lc3_cc_logic_1_n), .Z(lc3_cc_logic_1_z), .P(lc3_cc_logic_1_p));
  assign driver_1_out = GateMDR ? D_in : 16'bz;  // Driver driver_2
  LED Z_2 (.in(Z));
  Multiplexer #(.Bits(16)) multiplexer_4 (.sel(MIO_EN), .in_0(driver_1_out), .in_1(INMUX_out), .out(multiplexer_4_out));
  Register #(.Bits(16)) MDR (.D(multiplexer_4_out), .C(Clk), .en(LD_MDR), .Q(D_in));
  // Probe on D_in
  LED u_P (.in(P));
  Register P_2 (.D(lc3_cc_logic_1_p), .C(Clk), .en(LD_CC), .Q(P));
  lc3_control lc3_control_1 (
    .Clk(Clk), .INT(1'b0), .R(R), .IR_15_11({IR_15_11, DR_nzp[2]}), .BEN(BEN), .PSR_15(PSR_15), .ACV(ACV),
    .LD_MAR(LD_MAR), .LD_MDR(LD_MDR), .LD_IR(LD_IR), .LD_BEN(LD_BEN), .LD_REG(LD_REG), .LD_CC(LD_CC),
    .LD_PC(LD_PC), .LD_Priv(LD_Priv), .LD_SavedSSP(LD_SavedSSP), .LD_SavedUSP(LD_SavedUSP),
    .LD_Vector(LD_Vector), .LD_ACV(LD_ACV), .GatePC(GatePC), .GateMDR(GateMDR), .GateALU(GateALU),
    .GateMARMUX(GateMARMUX), .GateVector(GateVector), .GatePC_1(GatePC_1), .GatePSR(GatePSR),
    .GateSP(GateSP), .PCMUX(PCMUX), .DRMUX(DRMUX), .SR1MUX(SR1MUX), .ADDR2MUX(ADDR2MUX), .SPMUX(SPMUX),
    .ALUK(ALUK), .ADDR1MUX(ADDR1MUX), .MARMUX(MARMUX), .TableMUX(TableMux), .PSRMUX(PSRMux), .MIO_EN(MIO_EN),
    .R_W(R_W), .Set_Priv(Set_Priv), .State(State));  // open: LD_Priority, VectorMUX
  assign driver_1_out = GatePC_1 ? _1_s : 16'bz;  // Driver driver_3
  Add #(.Bits(16)) _1 (.a(PC), .b({16{1'b1}}), .c_i(1'b0), .s(_1_s));  // open: c_o
  // lc3_memory lc3_memory_1: pin names not known; wires that end beside it: R_mem, D_out, Clk, R_W, MEM_EN, D_in, MAR
  Multiplexer #(.Selector_Bits(2), .Bits(16)) multiplexer_5 (
    .sel(MDR_Select), .in_0(KBSR), .in_1(KBDR), .in_2(DSR), .in_3(D_out), .out(INMUX_out));
  lc3_memmap lc3_memmap_1 (
    .addr(MAR), .en(MIO_EN), .R_W(R_W), .MDR_Select(MDR_Select), .MEM_EN(MEM_EN), .LD_KBSR(LD_KBSR),
    .LD_DSR(LD_DSR), .LD_DDR(LD_DDR), .R_mapped(R_mapped));
  // Probe on PC
  Add #(.Bits(16)) plus_1 (.a(PC), .b(16'h1), .c_i(1'b0), .s(plus_1_s));  // open: c_o
  Multiplexer #(.Selector_Bits(2), .Bits(16)) multiplexer_6 (
    .sel(PCMUX), .in_0(plus_1_s), .in_1(driver_1_out), .in_2(lc3_alu_1_alu), .in_3({16{1'b0}}),
    .out(multiplexer_6_out));
  Register #(.Bits(16)) u_MAR (.D(driver_1_out), .C(Clk), .en(LD_MAR), .Q(MAR));
  // Probe on MAR
  assign driver_1_out = GatePC ? PC : 16'bz;  // Driver driver_4
  pc #(.applicationType("IVERILOG"), .CodeFile("/home/allan/cs061/LC3_realized/lc3-pc.v")) u_pc (
    .addr_in(multiplexer_6_out), .clk(Clk), .en(LD_PC), .addr_out(PC));
  Comparator #(.Bits(2)) comparator_4 (.a(2'b01), .b(MDR_Select), .eq(comparator_4_eq));  // open: gt, lt
  Keyboard keyboard_1 (.C(Clk), .en(comparator_4_eq), .D(keyboard_1_d), .av(KB_Data[15]));
  Register #(.Bits(16)) u_KBSR (.D({KB_Data[15], {15{1'b0}}}), .C(Clk), .en(KB_Data[15]), .Q(KBSR));
  Register #(.Bits(16)) u_KBDR (.D(keyboard_1_d), .C(Clk), .en(KB_Data[15]), .Q(KBDR));
  Multiplexer #(.Selector_Bits(2), .Bits(3)) multiplexer_7 (
    .sel(DRMUX), .in_0(DR_nzp), .in_1(3'b111), .in_2(3'b110), .in_3(3'b000), .out(multiplexer_7_out));
  BitExtender #(.inputBits(5)) SEXT_4 (.in(Immed), .out(SEXT_4_out));
  // Probe State on State
  lc3_register_file lc3_register_file_1 (
    .Clk(Clk), .Data(driver_1_out), .LD_Reg(LD_REG), .DR(multiplexer_7_out), .SR1(multiplexer_9_out),
    .SR2(Immed[2:0]), .SR2_OUT(lc3_register_file_1_sr2_out), .SR1_OUT(SR1_OUT));
  Multiplexer #(.Bits(16)) multiplexer_8 (
    .sel(SR2MUX), .in_0(lc3_register_file_1_sr2_out), .in_1(SEXT_4_out), .out(multiplexer_8_out));
  lc3_alu lc3_alu_2 (.ALU(lc3_alu_2_alu), .A(SR1_OUT), .B(multiplexer_8_out), .ALUK(ALUK));
  assign driver_1_out = GateALU ? lc3_alu_2_alu : 16'bz;  // Driver driver_5
  Multiplexer #(.Selector_Bits(2), .Bits(3)) multiplexer_9 (
    .sel(SR1MUX), .in_0(DR_nzp), .in_1(SR1), .in_2(3'b110), .in_3(3'b000), .out(multiplexer_9_out));
  Register #(.Bits(16)) u_DSR (.D(16'h8000), .C(Clk), .en(Clk), .Q(DSR));
  Terminal terminal_1 (.D(D_in[7:0]), .C(Clk), .en(LD_DDR));
  lc3_details lc3_details_1 (
    .Clk(Clk), .LD_SavedSSP(LD_SavedSSP), .LD_SavedUSP(LD_SavedUSP), .GateSP(GateSP), .SPMUX(SPMUX),
    .SR1_Val(SR1_OUT), .TableMux(TableMux), .LD_Vector(LD_Vector), .GateVector(GateVector), .N(N), .Z(Z),
    .P(P), .IR_2_0(DR_nzp), .LD_BEN(LD_BEN), .LD_ACV(LD_ACV), .Set_Priv(Set_Priv), .PSRMux(PSRMux),
    .GatePSR(GatePSR), .LD_Priv(LD_Priv), .Bus(driver_1_out), .GatedSP(driver_1_out),
    .GatedVector(driver_1_out), .GatedPSR(driver_1_out), .BEN(BEN), .ACV(ACV), .PSR_15(PSR_15));

  // Other names for the same wires on the sheet: SR2[2:0] = Immed[2:0]; IR_15_11[0] = DR_nzp[2]

  // Notes on the sheet:
  //   Breakpoint: default 65535
  //   Input
  //   Output
endmodule
