// Digital circuit lc3_HDL.dig as structural Verilog
module lc3_HDL (
  input  Clock,
  input  [15:0] Breakpoint,
  input  Enabled
);

  wire ACV, ADDR1MUX, BEN, Clk, GateALU, GateMARMUX, GateMDR, GatePC, GatePC_1, GatePSR, GateSP, GateVector,
       lc3_cc_logic_1_n, lc3_cc_logic_1_p, lc3_cc_logic_1_z, lc3_halt_hdl_1_p4, LD_ACV, LD_BEN, LD_CC,
       LD_DDR, LD_IR, LD_MAR, LD_MDR, LD_PC, LD_Priv, LD_REG, LD_SavedSSP, LD_SavedUSP, LD_Vector, MARMUX,
       MIO_EN, N, P, PSR_15, PSRMux, R, R_W, Set_Priv, SR2MUX, TableMux, Z;
  wire [1:0] ADDR2MUX, ALUK, DRMUX, PCMUX, SPMUX, SR1MUX;
  wire [2:0] IR_2_0, multiplexer_7_out, multiplexer_9_out, priorityencoder_1_num, SR1;
  wire [4:0] Immed;
  wire [4:1] IR_15_11;
  wire [5:0] State;
  wire [15:0] ADDER, ALU, Bus, DSR, KBDR, KBSR, lc3_register_file_1_sr2_out, MAR, MARMUX_OUT, MDR,
       Memory_d_out, multiplexer_2_out, multiplexer_3_out, multiplexer_4_out, multiplexer_5_out,
       multiplexer_8_out, PC, PC_1, plus_1_s, PSR, SEXT_2_out, SEXT_3_out, SEXT_4_out, SEXT_out, SP, SR1_OUT,
       Vector;

  Register #(.Bits(16)) IR (.D(Bus), .C(Clk), .en(LD_IR), .Q({IR_15_11, IR_2_0, SR1, SR2MUX, Immed}));
  BitExtender #(.inputBits(6)) SEXT (.in({SR2MUX, Immed}), .out(SEXT_out));
  BitExtender #(.inputBits(9)) SEXT_2 (.in({SR1, SR2MUX, Immed}), .out(SEXT_2_out));
  BitExtender #(.inputBits(11)) SEXT_3 (.in({IR_2_0[1:0], SR1, SR2MUX, Immed}), .out(SEXT_3_out));
  // lc3_halt_HDL lc3_halt_hdl_1: pin names not known; wires that end beside it: MAR, MDR, R_W, lc3_halt_hdl_1_p4
  Multiplexer #(.Bits(16)) multiplexer_1 (
    .sel(MARMUX), .in_0({{8{1'b0}}, SR1[1:0], SR2MUX, Immed}), .in_1(ADDER), .out(MARMUX_OUT));
  lc3_breakpoint lc3_breakpoint_1 (.Breakpoint(Breakpoint), .PC(PC), .State(State), .en(Enabled));
  Multiplexer #(.Selector_Bits(2), .Bits(16)) multiplexer_2 (
    .sel(ADDR2MUX), .in_0({16{1'b0}}), .in_1(SEXT_out), .in_2(SEXT_2_out), .in_3(SEXT_3_out),
    .out(multiplexer_2_out));
  Register register_1 (.D(lc3_cc_logic_1_n), .C(Clk), .en(LD_CC), .Q(N));
  lc3_cc_logic lc3_cc_logic_1 (.D_in(Bus), .N(lc3_cc_logic_1_n), .Z(lc3_cc_logic_1_z), .P(lc3_cc_logic_1_p));
  and and_1 (Clk, Clock, lc3_halt_hdl_1_p4);
  Multiplexer #(.Bits(16)) multiplexer_3 (.sel(ADDR1MUX), .in_0(PC), .in_1(SR1_OUT), .out(multiplexer_3_out));
  Register register_2 (.D(lc3_cc_logic_1_z), .C(Clk), .en(LD_CC), .Q(Z));
  lc3_alu lc3_alu_1 (.ALU(ADDER), .A(multiplexer_2_out), .B(multiplexer_3_out), .ALUK(2'b00));
  Register register_3 (.D(lc3_cc_logic_1_p), .C(Clk), .en(LD_CC), .Q(P));
  lc3_control lc3_control_1 (
    .Clk(Clk), .INT(1'b0), .R(R), .IR_15_11({IR_15_11, IR_2_0[2]}), .BEN(BEN), .PSR_15(PSR_15), .ACV(ACV),
    .LD_MAR(LD_MAR), .LD_MDR(LD_MDR), .LD_IR(LD_IR), .LD_BEN(LD_BEN), .LD_REG(LD_REG), .LD_CC(LD_CC),
    .LD_PC(LD_PC), .LD_Priv(LD_Priv), .LD_SavedSSP(LD_SavedSSP), .LD_SavedUSP(LD_SavedUSP),
    .LD_Vector(LD_Vector), .LD_ACV(LD_ACV), .GatePC(GatePC), .GateMDR(GateMDR), .GateALU(GateALU),
    .GateMARMUX(GateMARMUX), .GateVector(GateVector), .GatePC_1(GatePC_1), .GatePSR(GatePSR),
    .GateSP(GateSP), .PCMUX(PCMUX), .DRMUX(DRMUX), .SR1MUX(SR1MUX), .ADDR2MUX(ADDR2MUX), .SPMUX(SPMUX),
    .ALUK(ALUK), .ADDR1MUX(ADDR1MUX), .MARMUX(MARMUX), .TableMUX(TableMux), .PSRMUX(PSRMux), .MIO_EN(MIO_EN),
    .R_W(R_W), .Set_Priv(Set_Priv), .State(State));
  Register #(.Bits(16)) u_MDR (.D(multiplexer_4_out), .C(Clk), .en(LD_MDR), .Q(MDR));
  Add #(.Bits(16)) _1 (.a(PC), .b({16{1'b1}}), .c_i(1'b0), .s(PC_1));  // open: c_o
  Multiplexer #(.Bits(16)) multiplexer_4 (.sel(MIO_EN), .in_0(Bus), .in_1(Memory_d_out), .out(multiplexer_4_out));
  Add #(.Bits(16)) plus_1 (.a(PC), .b(16'h1), .c_i(1'b0), .s(plus_1_s));  // open: c_o
  Multiplexer #(.Selector_Bits(2), .Bits(16)) multiplexer_5 (
    .sel(PCMUX), .in_0(plus_1_s), .in_1(Bus), .in_2(ADDER), .in_3({16{1'b0}}), .out(multiplexer_5_out));
  lc3_memory Memory (
    .Addr(MAR), .D_in(MDR), .R_W(R_W), .Clk(Clk), .MIO_EN(MIO_EN), .KBSR(KBSR), .KBDR(KBDR), .DSR(DSR),
    .D_out(Memory_d_out), .R(R), .LD_DDR(LD_DDR));  // open: LD_KBSR, LD_DSR
  pc #(.applicationType("IVERILOG"), .CodeFile(".\\lc3-pc.v")) u_pc (
    .D(multiplexer_5_out), .C(Clk), .en(LD_PC), .Q(PC));
  Register #(.Bits(16)) u_MAR (.D(Bus), .C(Clk), .en(LD_MAR), .Q(MAR));
  Multiplexer #(.Bits(16), .Selector_Bits(3)) multiplexer_6 (
    .sel(priorityencoder_1_num), .in_0(MARMUX_OUT), .in_1(PC_1), .in_2(PC), .in_3(ALU), .in_4(MDR),
    .in_5(PSR), .in_6(Vector), .in_7(SP), .out(Bus));
  PriorityEncoder #(.Selector_Bits(3)) priorityencoder_1 (
    .in0(GateMARMUX), .in1(GatePC_1), .in2(GatePC), .in3(GateALU), .in4(GateMDR), .in5(GatePSR),
    .in6(GateVector), .in7(GateSP), .num(priorityencoder_1_num));  // open: any
  lc3_input_HDL lc3_input_hdl_1 (.Addr(MAR), .Clk(Clk), .KBSR(KBSR), .KBDR(KBDR));
  Multiplexer #(.Selector_Bits(2), .Bits(3)) multiplexer_7 (
    .sel(DRMUX), .in_0(IR_2_0), .in_1(3'b111), .in_2(3'b110), .in_3(3'b000), .out(multiplexer_7_out));
  BitExtender #(.inputBits(5)) SEXT_4 (.in(Immed), .out(SEXT_4_out));
  lc3_register_file lc3_register_file_1 (
    .Clk(Clk), .Data(Bus), .LD_Reg(LD_REG), .DR(multiplexer_7_out), .SR1(multiplexer_9_out),
    .SR2(Immed[2:0]), .SR2_OUT(lc3_register_file_1_sr2_out), .SR1_OUT(SR1_OUT));
  lc3_alu lc3_alu_2 (.ALU(ALU), .A(SR1_OUT), .B(multiplexer_8_out), .ALUK(ALUK));
  Multiplexer #(.Bits(16)) multiplexer_8 (
    .sel(SR2MUX), .in_0(lc3_register_file_1_sr2_out), .in_1(SEXT_4_out), .out(multiplexer_8_out));
  // Probe on PCMUX
  // Probe on DRMUX
  // Probe on SR1MUX
  // Probe on SR2MUX
  // Probe on ADDR1MUX
  // Probe on ADDR2MUX
  // Probe on SPMUX
  // Probe on ALUK
  // Probe on State
  Multiplexer #(.Selector_Bits(2), .Bits(3)) multiplexer_9 (
    .sel(SR1MUX), .in_0(IR_2_0), .in_1(SR1), .in_2(3'b110), .in_3(3'b000), .out(multiplexer_9_out));
  lc3_output_HDL lc3_output_hdl_1 (.D(MDR), .Clk(Clk), .en(LD_DDR), .DSR(DSR));
  lc3_details_HDL lc3_details_hdl_1 (
    .Clk(Clk), .LD_SavedSSP(LD_SavedSSP), .LD_SavedUSP(LD_SavedUSP), .SPMUX(SPMUX), .SR1_Val(SR1_OUT),
    .TableMux(TableMux), .LD_Vector(LD_Vector), .N(N), .Z(Z), .P(P), .IR_2_0(IR_2_0), .LD_BEN(LD_BEN),
    .LD_ACV(LD_ACV), .Set_Priv(Set_Priv), .PSRMux(PSRMux), .LD_Priv(LD_Priv), .Bus(Bus), .SP(SP),
    .Vector(Vector), .PSR(PSR), .BEN(BEN), .ACV(ACV), .PSR_15(PSR_15));

  // Other names for the same wires on the sheet: SR2[2:0] = Immed[2:0]; IR_15_11[0] = IR_2_0[2]; MDR_out[15:0] = MDR

  // Notes on the sheet:
  //   Breakpoint: default 12288
  //   Debug/Controls
  //   Input
  //   Output
endmodule
